// Logisim project Ctl_Conditional.circ as structural Verilog: 1 circuit, main circuit Conditional
module Conditional (
  input  Enable,
  input  [15:0] Instruction,
  input  Z,
  input  C,
  input  N,
  input  V,
  output [10:0] Offset,
  output Verified
);

  wire and_3_out, and_4_out, Ci, Ni, not_1_out, not_2_out, not_3_out, not_4_out, not_5_out, or_1_out, res8,
       res9, res10, res11, res12, res13, Verified_t, xnor_1_out, xnor_2_out, Zi;

  Multiplexer #(.select(4)) multiplexer_1 (
    .in0(1'b0), .in1(1'b0), .in2(1'b1), .in3(1'b0), .in4(1'b0), .in5(1'b0), .in6(1'b0), .in7(1'b0),
    .in8(1'b0), .in9(1'b0), .in10(1'b0), .in11(1'b0), .in12(1'b0), .in13(1'b0), .in14(1'b0), .in15(1'b0),
    .out(Ci), .sel(Instruction[7:4]));
  Multiplexer #(.select(4)) multiplexer_2 (
    .in0(1'b1), .in1(1'b0), .in2(1'b0), .in3(1'b0), .in4(1'b0), .in5(1'b0), .in6(1'b0), .in7(1'b0),
    .in8(1'b0), .in9(1'b0), .in10(1'b0), .in11(1'b0), .in12(1'b0), .in13(1'b0), .in14(1'b0), .in15(1'b0),
    .out(Zi), .sel(Instruction[7:4]));
  and and_1 (Verified_t, Ci, Zi, Ni, res8, res8, res9, res10, res11, res12, res13);
  Multiplexer #(.select(4)) multiplexer_3 (
    .in0(1'b0), .in1(1'b0), .in2(1'b0), .in3(1'b0), .in4(1'b1), .in5(1'b0), .in6(1'b0), .in7(1'b0),
    .in8(1'b0), .in9(1'b0), .in10(1'b0), .in11(1'b0), .in12(1'b0), .in13(1'b0), .in14(1'b0), .in15(1'b0),
    .out(Ni), .sel(Instruction[7:4]));
  and and_2 (Verified, Enable, Verified_t);
  Multiplexer #(.select(4)) multiplexer_4 (
    .in0(1'b0), .in1(1'b0), .in2(1'b0), .in3(1'b0), .in4(1'b0), .in5(1'b0), .in6(1'b1), .in7(1'b0),
    .in8(1'b0), .in9(1'b0), .in10(1'b0), .in11(1'b0), .in12(1'b0), .in13(1'b0), .in14(1'b0), .in15(1'b0),
    .out(res8), .sel(Instruction[7:4]));
  not not_1 (not_1_out, C);
  or or_1 (or_1_out, not_1_out, Z);
  Multiplexer #(.select(4)) multiplexer_5 (
    .in0(1'b0), .in1(1'b0), .in2(1'b0), .in3(1'b0), .in4(1'b0), .in5(1'b0), .in6(1'b0), .in7(1'b0),
    .in8(1'b0), .in9(or_1_out), .in10(1'b0), .in11(1'b0), .in12(1'b0), .in13(1'b0), .in14(1'b0), .in15(1'b0),
    .out(res9), .sel(Instruction[7:4]));
  and and_3 (and_3_out, C, not_2_out);
  not not_2 (not_2_out, Z);
  Multiplexer #(.select(4)) multiplexer_6 (
    .in0(1'b0), .in1(1'b0), .in2(1'b0), .in3(1'b0), .in4(1'b0), .in5(1'b0), .in6(1'b0), .in7(1'b0),
    .in8(and_3_out), .in9(1'b0), .in10(1'b0), .in11(1'b0), .in12(1'b0), .in13(1'b0), .in14(1'b0),
    .in15(1'b0), .out(res8), .sel(Instruction[7:4]));
  xnor xnor_1 (xnor_1_out, N, V);
  Multiplexer #(.select(4)) multiplexer_7 (
    .in0(1'b0), .in1(1'b0), .in2(1'b0), .in3(1'b0), .in4(1'b0), .in5(1'b0), .in6(1'b0), .in7(1'b0),
    .in8(1'b0), .in9(1'b0), .in10(xnor_1_out), .in11(1'b0), .in12(1'b0), .in13(1'b0), .in14(1'b0),
    .in15(1'b0), .out(res10), .sel(Instruction[7:4]));
  xnor xnor_2 (xnor_2_out, N, V);
  not not_3 (not_3_out, xnor_2_out);
  Multiplexer #(.select(4)) multiplexer_8 (
    .in0(1'b0), .in1(1'b0), .in2(1'b0), .in3(1'b0), .in4(1'b0), .in5(1'b0), .in6(1'b0), .in7(1'b0),
    .in8(1'b0), .in9(1'b0), .in10(1'b0), .in11(not_3_out), .in12(1'b0), .in13(1'b0), .in14(1'b0),
    .in15(1'b0), .out(res11), .sel(Instruction[7:4]));
  not not_4 (not_4_out, Z);
  and and_4 (and_4_out, not_4_out, res11);
  Multiplexer #(.select(4)) multiplexer_9 (
    .in0(1'b0), .in1(1'b0), .in2(1'b0), .in3(1'b0), .in4(1'b0), .in5(1'b0), .in6(1'b0), .in7(1'b0),
    .in8(1'b0), .in9(1'b0), .in10(1'b0), .in11(1'b0), .in12(and_4_out), .in13(1'b0), .in14(1'b0),
    .in15(1'b0), .out(res12), .sel(Instruction[7:4]));
  not not_5 (not_5_out, res12);
  Multiplexer #(.select(4)) multiplexer_10 (
    .in0(1'b0), .in1(1'b0), .in2(1'b0), .in3(1'b0), .in4(1'b0), .in5(1'b0), .in6(1'b0), .in7(1'b0),
    .in8(1'b0), .in9(1'b0), .in10(1'b0), .in11(1'b0), .in12(1'b0), .in13(not_5_out), .in14(1'b0),
    .in15(1'b0), .out(res13), .sel(Instruction[7:4]));

  // Other names for the same wires on the sheet: Inst[3:0] = Instruction[7:4]; Vi = res8
endmodule
