// Logisim project Ctl_Flags_APSR.circ as structural Verilog: 1 circuit, main circuit Flags_APSR
module Flags_APSR (
  input  [3:0] Update_Mask,
  input  [3:0] Flags_In,
  input  Rst,
  input  Clk,
  output [3:0] Flags_Out
);

  wire [3:0] and_1_out, register_1_q;

  assign and_1_out = Update_Mask & Flags_In;  // AND_Gate and_1, 4 bits wide
  Register #(.width(4)) register_1 (.en(Rst), .clk(Clk), .Q(register_1_q));  // open: D, clr
  assign Flags_Out = and_1_out | register_1_q;  // OR_Gate or_1, 4 bits wide
endmodule
